# Fritzing sketch circuit (saved by Fritzing 0.9.3b)
breadboards: 1

parts:
  Componente1 = Arduino Uno (Rev3)
  LED1 = RGB LED (com. cathode, rgb) [package="5 mm [THT]"]
  Componente2 = Arduino Joystick Shield

nets:
  N1: Componente1.D9_PWM, LED1.blue_anode
  N2: Componente1.D10_PWM/SS, LED1.green_anode
  N3: Componente1.D11_PWM/MOSI, LED1.red_anode
  N4: Componente1.D2, Componente2.SEL
  N5: Componente1.D3_PWM, Componente2.D3
  N6: Componente1.D4, Componente2.D4
  5V: Componente1.5V, Componente2.5V
  N7: Componente1.GND, LED1.common_cathode
